# Fritzing sketch project2 (saved by Fritzing 0.9.3b)
circuit board: 8.46667cm x 5.64444cm
breadboards: 1

parts:
  Part1 = Arduino Uno (Rev3) - ICSP
  R1 = Resistor [tolerance=±5% resistance=2.2k package=THT]
  R2 = Resistor [tolerance=±5% resistance=2.2k package=THT]
  part = DHT11 Humitidy and Temperature Sensor

nets (from the schematic view):
  5V: Part1.5V, R2.Pin_1, part.VDD
  GND: Part1.GND, part.GND
  N1: Part1.D13/SCK, R1.Pin_0, part.DATA
  N2: R1.Pin_1, R2.Pin_0

custom parts:
  DHT11 Humitidy and Temperature Sensor: DHT11 Humidity and Temperature Sensor
